# Fritzing sketch KeyboardLED (saved by Fritzing 0.9.3b)
perfboards: 1

parts:
  Digispark1 = Digispark
  Q1 = Basic FET N-Channel [package="TO220 [THT]"]
  R1 = Resistor [tolerance=±5% resistance=10k package=THT]
  JP1 = Header 1 [package=snap-female]
  JP2 = Header 1 [package=snap-female]
  JP3 = Header 1 [package=snap-female]
  JP4 = Header 1 [package=snap-female]
  JP5 = Header 1 [package=snap-female]  # not connected
  U2 = Vibration Motor- ROB-08449 [package=vibe-motor-10mm]  # not connected
  U3 = Vibration Motor- ROB-08449 [package=vibe-motor-10mm]  # not connected
  U4 = Vibration Motor- ROB-08449 [package=vibe-motor-10mm]  # not connected
  U5 = Vibration Motor- ROB-08449 [package=vibe-motor-10mm]  # not connected
  U1 = Vibration Motor- ROB-08449 [package=vibe-motor-10mm]  # not connected

nets:
  N1: Digispark1.VCC, JP3.1, JP4.1
  N2: Digispark1.GND, Q1.source, R1.Pin_1, JP1.1
  N3: Digispark1.P0, Q1.gate, R1.Pin_0
  N4: Digispark1.P2, JP2.1

custom parts:
  Digispark: The Digispark is an Attiny85 based microcontroller development board similar to the Arduino line, only cheaper, smaller, and a bit less powerful. With a whole host of shields to extend its functionality and the ability to use the familiar Arduino IDE the Digispark is a great way to jump into electronics, or perfect for when an Arduino is too big or too much.
