# Fritzing sketch tracer_la_lune_glove (saved by Fritzing 0.9.3b)
breadboards: 1
stripboards: 1

parts:
  U1 = attiny85 [package=dip]
  Q1 = Basic FET N-Channel [package="TO220 [THT]"]
  D2 = Rectifier Diode [part_number=1N4001 package="300 mil [THT]"]
  U2 = Vibration Motor- ROB-08449 [package=vibe-motor-10mm]
  R1 = Rotary Potentiometer (Small) [maximum_resistance=50kΩ package=THT]
  R2 = Resistor [tolerance=±5% resistance=220 package="1206 [SMD]"]
  C1 = Electrolytic Capacitor [capacitance=100µF package="200 mil [THT, electrolytic]"]

nets:
  GND: U1.Pin_4, D2.anode, U2.-, R1.leg1, R2.Pin_0, C1.-
  N1: U1.Pin_5, Q1.gate, R2.Pin_1
  N2: U1.Pin_7, R1.wiper
  5V: U1.Pin_8, Q1.drain, R1.leg2, C1.+
  N3: Q1.source, D2.cathode, U2.+
